// Digital circuit CPU.dig as structural Verilog
module CPU (
  input  [15:0] inM,
  input  [15:0] instruction,
  input  reset,
  input  clock,
  output [15:0] outM,
  output writeM,
  output [15:0] pc,
  output [15:0] addressM
);

  wire and_1_out, and_2_out, and_3_out, and_4_out, demultiplexer_1_out_1, ng, or_1_out, or_2_out, zr;
  wire [15:0] alu16_1_out, D_Register_q, multiplexer_1_out, multiplexer_2_out;

  Multiplexer #(.Bits(16)) multiplexer_1 (
    .sel(instruction[15]), .in_0(instruction), .in_1(outM), .out(multiplexer_1_out));
  or or_1 (or_1_out, ~instruction[15], instruction[5]);  // Or
  Register #(.Bits(16)) A_Register (.D(multiplexer_1_out), .C(clock), .en(or_1_out), .Q(addressM));
  and and_1 (and_1_out, instruction[2], ng);
  and and_2 (and_2_out, instruction[1], zr);
  and and_3 (and_3_out, instruction[0], ~ng, ~zr);  // And
  and and_4 (and_4_out, instruction[15], instruction[4]);
  Multiplexer #(.Bits(16)) multiplexer_2 (.sel(instruction[12]), .in_0(addressM), .in_1(inM), .out(multiplexer_2_out));
  or or_2 (or_2_out, and_1_out, and_2_out, and_3_out);
  Register #(.Bits(16)) D_Register (.D(outM), .C(clock), .en(and_4_out), .Q(D_Register_q));
  alu16 alu16_1 (
    .zx(instruction[11]), .nx(instruction[10]), .zy(instruction[9]), .ny(instruction[8]), .f(instruction[7]),
    .no(instruction[6]), .out(alu16_1_out), .zr(zr), .ng(ng), .x(D_Register_q), .y(multiplexer_2_out));
  Demultiplexer demultiplexer_1 (.sel(instruction[15]), .in(or_2_out), .out_1(demultiplexer_1_out_1));  // open: out_0
  pc pc_1 (.in(addressM), .inc(1'b1), .en(demultiplexer_1_out_1), .reset(reset), .clock(clock), .out(pc));
  Demultiplexer #(.Bits(16)) demultiplexer_2 (.sel(instruction[15]), .in(alu16_1_out), .out_1(outM));  // open: out_0
  Demultiplexer demultiplexer_3 (.sel(instruction[15]), .in(instruction[3]), .out_1(writeM));  // open: out_0

  // Notes on the sheet:
  //   instruction: default 1
endmodule
