// Digital circuit Dmux.dig as structural Verilog
module Dmux (
  input  sel,
  input  in,
  output b,
  output a
);

  wire not_1_out;

  not not_1 (not_1_out, sel);
  and and_1 (a, in, not_1_out);
  and and_2 (b, in, sel);
endmodule
