// Digital circuit Dmux4Way.dig as structural Verilog
module Dmux4Way (
  input  [1:0] sel,
  input  in,
  output b,
  output a,
  output d,
  output c
);

  wire and_1_out, and_2_out, and_3_out, and_4_out, not_1_out, not_2_out, not_3_out, not_4_out;

  not not_1 (not_1_out, sel[0]);
  not not_2 (not_2_out, sel[1]);
  not not_3 (not_3_out, sel[1]);
  not not_4 (not_4_out, sel[0]);
  and and_1 (and_1_out, not_1_out, not_2_out);
  and and_2 (and_2_out, sel[0], not_3_out);
  and and_3 (and_3_out, not_4_out, sel[1]);
  and and_4 (and_4_out, sel[0], sel[1]);
  and and_5 (a, in, and_1_out);
  and and_6 (b, in, and_2_out);
  and and_7 (c, in, and_3_out);
  and and_8 (d, in, and_4_out);
endmodule
