// Digital circuit Dmux8Way.dig as structural Verilog
module Dmux8Way (
  input  [2:0] sel,
  input  in,
  output b,
  output a,
  output d,
  output c,
  output f,
  output e,
  output h,
  output g
);

  wire and_1_out, and_2_out, and_3_out, and_4_out, and_5_out, and_6_out, and_7_out, and_8_out, and_9_out,
       and_10_out, and_11_out, and_12_out, and_13_out, and_14_out, and_15_out, and_16_out, not_1_out,
       not_2_out, not_3_out, not_4_out, not_5_out, not_6_out, not_7_out, not_8_out, not_9_out, not_10_out,
       not_11_out, not_12_out;

  not not_1 (not_1_out, sel[2]);
  not not_2 (not_2_out, sel[1]);
  not not_3 (not_3_out, sel[0]);
  not not_4 (not_4_out, sel[2]);
  not not_5 (not_5_out, sel[1]);
  not not_6 (not_6_out, sel[2]);
  not not_7 (not_7_out, sel[0]);
  not not_8 (not_8_out, sel[2]);
  not not_9 (not_9_out, sel[1]);
  not not_10 (not_10_out, sel[0]);
  not not_11 (not_11_out, sel[1]);
  not not_12 (not_12_out, sel[0]);
  and and_1 (and_1_out, not_2_out, not_3_out);
  and and_2 (and_2_out, not_5_out, sel[0]);
  and and_3 (and_3_out, sel[1], not_7_out);
  and and_4 (and_4_out, sel[1], sel[0]);
  and and_5 (and_5_out, not_9_out, not_10_out);
  and and_6 (and_6_out, not_11_out, sel[0]);
  and and_7 (and_7_out, sel[1], not_12_out);
  and and_8 (and_8_out, sel[1], sel[2]);
  and and_9 (and_9_out, not_1_out, and_1_out);
  and and_10 (and_10_out, not_4_out, and_2_out);
  and and_11 (and_11_out, not_6_out, and_3_out);
  and and_12 (and_12_out, not_8_out, and_4_out);
  and and_13 (and_13_out, sel[2], and_5_out);
  and and_14 (and_14_out, sel[2], and_6_out);
  and and_15 (and_15_out, sel[2], and_7_out);
  and and_16 (and_16_out, sel[0], and_8_out);
  and and_17 (a, in, and_9_out);
  and and_18 (b, in, and_10_out);
  and and_19 (c, in, and_11_out);
  and and_20 (d, in, and_12_out);
  and and_21 (e, in, and_13_out);
  and and_22 (f, in, and_14_out);
  and and_23 (g, in, and_15_out);
  and and_24 (h, in, and_16_out);
endmodule
