// Digital circuit HackComputer.dig as structural Verilog
module HackComputer (
  input  reset,
  input  clk
);

  wire cpu_1_p6;
  wire [15:0] cpu_1_p5, cpu_1_p7, cpu_1_p8, ramdualport_1_d, rom_1_d;

  RAMDualPort #(.AddrBits(16), .Bits(16)) ramdualport_1 (
    .A(cpu_1_p8), .Din(cpu_1_p5), .str(cpu_1_p6), .C(clk), .ld(1'b1), .D(ramdualport_1_d));
  ROM #(.AddrBits(16), .isProgramMemory("true"), .Bits(16)) rom_1 (.A(cpu_1_p7), .sel(1'b1), .D(rom_1_d));
  // CPU cpu_1: pin names not known; wires that end beside it: clk, ramdualport_1_d, rom_1_d, reset, cpu_1_p5, cpu_1_p6, cpu_1_p7, cpu_1_p8

  // Notes on the sheet:
  //   clk: Hz: 2147483647
  //   contents of rom_1 (hex, n*v repeats v):
  //   fdc8,ec10,0,e308,10,efc8,11,ea88,10,fc10,0,f4d0,19,e301,11,fc10
  //   ,10,f090,11,e308,10,fc10,e7c8,8,ea87,11,fc10,1,e308,1d,ea87
endmodule
