// Digital circuit ICs.dig as structural Verilog
module ICs (
);

  // NAnd nand_1 is placed but not wired
  // Not not_1 is placed but not wired
  // And and_1 is placed but not wired
  // Or or_1 is placed but not wired
  // XOr xor_1 is placed but not wired
  Not not_2 ();  // open: in, out
  And and_2 ();  // open: a, b, out
  Or or_2 ();  // open: a, b, out
  Xor xor_2 ();  // open: a, b, out
  Mux mux_1 ();  // open: a, b, sel, out
  Mux16 mux16_1 ();  // open: a, b, sel, out
  Mux4Way16 mux4way16_1 ();  // open: a, b, c, d, sel, out
  Mux8Way16 mux8way16_1 ();  // open: sel, a, b, c, d, e, f, g, h, out
  Dmux dmux_1 ();  // open: a, b, in, sel
  Dmux4Way dmux4way_1 ();  // open: a, b, c, d, in, sel
  Dmux8Way dmux8way_1 ();  // open: a, b, c, d, e, f, g, h, sel, in
  Not16 not16_1 ();  // open: out, in
  And16 and16_1 ();  // open: a, b, out
  Or16 or16_1 ();  // open: a, b, out
  Or8Way or8way_1 ();  // open: _0, _1, _2, _3, _4, _5, _6, _7, out
endmodule
