// Digital circuit Mux16.dig as structural Verilog
module Mux16 (
  input  [15:0] a,
  input  [15:0] b,
  input  sel,
  output [15:0] out
);

  wire [15:0] and_1_out, and_2_out, not_1_out, split16_1_out;

  Split16 split16_1 (.in(sel), .out(split16_1_out));
  assign not_1_out = ~split16_1_out;  // Not not_1, 16 bits wide
  assign and_1_out = a & not_1_out;  // And and_1, 16 bits wide
  assign and_2_out = b & split16_1_out;  // And and_2, 16 bits wide
  assign out = and_1_out | and_2_out;  // Or or_1, 16 bits wide
endmodule
