// Digital circuit Mux4Way16.dig as structural Verilog
module Mux4Way16 (
  input  [15:0] a,
  input  [15:0] b,
  input  [1:0] sel,
  input  [15:0] c,
  input  [15:0] d,
  output [15:0] out
);

  wire [15:0] and_1_out, and_2_out, and_3_out, and_4_out, and_5_out, and_6_out, and_7_out, and_8_out,
       not_1_out, not_2_out, not_3_out, not_4_out, or_1_out, or_2_out, split16_1_out, split16_2_out;

  Split16 split16_1 (.in(sel[0]), .out(split16_1_out));
  Split16 split16_2 (.in(sel[1]), .out(split16_2_out));
  assign not_1_out = ~split16_1_out;  // Not not_1, 16 bits wide
  assign not_2_out = ~split16_2_out;  // Not not_2, 16 bits wide
  assign not_3_out = ~split16_2_out;  // Not not_3, 16 bits wide
  assign not_4_out = ~split16_1_out;  // Not not_4, 16 bits wide
  assign and_1_out = not_1_out & not_2_out;  // And and_1, 16 bits wide
  assign and_2_out = split16_1_out & not_3_out;  // And and_2, 16 bits wide
  assign and_3_out = not_4_out & split16_2_out;  // And and_3, 16 bits wide
  assign and_4_out = split16_1_out & split16_2_out;  // And and_4, 16 bits wide
  assign and_5_out = a & and_1_out;  // And and_5, 16 bits wide
  assign and_6_out = b & and_2_out;  // And and_6, 16 bits wide
  assign and_7_out = c & and_3_out;  // And and_7, 16 bits wide
  assign and_8_out = d & and_4_out;  // And and_8, 16 bits wide
  assign or_1_out = and_5_out | and_6_out;  // Or or_1, 16 bits wide
  assign or_2_out = and_7_out | and_8_out;  // Or or_2, 16 bits wide
  assign out = or_1_out | or_2_out;  // Or or_3, 16 bits wide
endmodule
