// Digital circuit Mux8Way16.dig as structural Verilog
module Mux8Way16 (
  input  [15:0] a,
  input  [15:0] b,
  input  [2:0] sel,
  input  [15:0] c,
  input  [15:0] d,
  input  [15:0] e,
  input  [15:0] f,
  input  [15:0] g,
  input  [15:0] h,
  output [15:0] out
);

  wire [15:0] and_1_out, and_2_out, and_3_out, and_4_out, and_5_out, and_6_out, and_7_out, and_8_out,
       and_9_out, and_10_out, and_11_out, and_12_out, and_13_out, and_14_out, and_15_out, and_16_out,
       and_17_out, and_18_out, and_19_out, and_20_out, and_21_out, and_22_out, and_23_out, and_24_out,
       not_1_out, not_2_out, not_3_out, not_4_out, not_5_out, not_6_out, not_7_out, not_8_out, not_9_out,
       not_10_out, not_11_out, not_12_out, or_1_out, or_2_out, or_3_out, or_4_out, or_5_out, or_6_out,
       split16_1_out, split16_2_out, split16_3_out;

  assign not_1_out = ~split16_1_out;  // Not not_1, 16 bits wide
  assign and_1_out = not_2_out & not_3_out;  // And and_1, 16 bits wide
  assign not_2_out = ~split16_2_out;  // Not not_2, 16 bits wide
  assign not_3_out = ~split16_3_out;  // Not not_3, 16 bits wide
  assign not_4_out = ~split16_1_out;  // Not not_4, 16 bits wide
  assign and_2_out = not_5_out & split16_3_out;  // And and_2, 16 bits wide
  assign not_5_out = ~split16_2_out;  // Not not_5, 16 bits wide
  assign not_6_out = ~split16_1_out;  // Not not_6, 16 bits wide
  assign and_3_out = split16_2_out & not_7_out;  // And and_3, 16 bits wide
  assign not_7_out = ~split16_3_out;  // Not not_7, 16 bits wide
  assign not_8_out = ~split16_1_out;  // Not not_8, 16 bits wide
  assign and_4_out = split16_2_out & split16_3_out;  // And and_4, 16 bits wide
  assign and_5_out = not_9_out & not_10_out;  // And and_5, 16 bits wide
  assign not_9_out = ~split16_2_out;  // Not not_9, 16 bits wide
  assign not_10_out = ~split16_3_out;  // Not not_10, 16 bits wide
  assign and_6_out = not_11_out & split16_3_out;  // And and_6, 16 bits wide
  assign not_11_out = ~split16_2_out;  // Not not_11, 16 bits wide
  assign and_7_out = split16_2_out & not_12_out;  // And and_7, 16 bits wide
  assign not_12_out = ~split16_3_out;  // Not not_12, 16 bits wide
  assign and_8_out = split16_2_out & split16_3_out;  // And and_8, 16 bits wide
  Split16 split16_1 (.in(sel[2]), .out(split16_1_out));
  Split16 split16_2 (.in(sel[1]), .out(split16_2_out));
  Split16 split16_3 (.in(sel[0]), .out(split16_3_out));
  assign and_9_out = not_1_out & and_1_out;  // And and_9, 16 bits wide
  assign and_10_out = not_4_out & and_2_out;  // And and_10, 16 bits wide
  assign and_11_out = not_6_out & and_3_out;  // And and_11, 16 bits wide
  assign and_12_out = not_8_out & and_4_out;  // And and_12, 16 bits wide
  assign and_13_out = split16_1_out & and_5_out;  // And and_13, 16 bits wide
  assign and_14_out = split16_1_out & and_6_out;  // And and_14, 16 bits wide
  assign and_15_out = split16_1_out & and_7_out;  // And and_15, 16 bits wide
  assign and_16_out = split16_1_out & and_8_out;  // And and_16, 16 bits wide
  assign and_17_out = a & and_9_out;  // And and_17, 16 bits wide
  assign and_18_out = b & and_10_out;  // And and_18, 16 bits wide
  assign and_19_out = c & and_11_out;  // And and_19, 16 bits wide
  assign and_20_out = d & and_12_out;  // And and_20, 16 bits wide
  assign and_21_out = e & and_13_out;  // And and_21, 16 bits wide
  assign and_22_out = f & and_14_out;  // And and_22, 16 bits wide
  assign and_23_out = g & and_15_out;  // And and_23, 16 bits wide
  assign and_24_out = h & and_16_out;  // And and_24, 16 bits wide
  assign or_1_out = and_17_out | and_18_out;  // Or or_1, 16 bits wide
  assign or_2_out = and_19_out | and_20_out;  // Or or_2, 16 bits wide
  assign or_3_out = and_21_out | and_22_out;  // Or or_3, 16 bits wide
  assign or_4_out = and_23_out | and_24_out;  // Or or_4, 16 bits wide
  assign or_5_out = or_1_out | or_2_out;  // Or or_5, 16 bits wide
  assign or_6_out = or_3_out | or_4_out;  // Or or_6, 16 bits wide
  assign out = or_5_out | or_6_out;  // Or or_7, 16 bits wide
endmodule
