// Digital circuit Or8Way.dig as structural Verilog
module Or8Way (
  input  _0,
  input  _1,
  input  _2,
  input  _3,
  input  _4,
  input  _5,
  input  _6,
  input  _7,
  output out
);

  wire or_1_out, or_2_out, or_3_out, or_4_out, or_5_out, or_6_out;

  or or_1 (or_1_out, _0, _1);
  or or_2 (or_2_out, or_1_out, _2);
  or or_3 (or_3_out, or_2_out, _3);
  or or_4 (or_4_out, or_3_out, _4);
  or or_5 (or_5_out, or_4_out, _5);
  or or_6 (or_6_out, or_5_out, _6);
  or or_7 (out, or_6_out, _7);
endmodule
