// Digital circuit Xor.dig as structural Verilog
module Xor (
  input  a,
  input  b,
  output out
);

  wire and_1_out, not_1_out, or_1_out;

  or or_1 (or_1_out, a, b);
  and and_1 (and_1_out, a, b);
  not not_1 (not_1_out, and_1_out);
  and and_2 (out, or_1_out, not_1_out);
endmodule
