// Digital circuit alu16.dig as structural Verilog
module alu16 (
  input  zx,
  input  nx,
  input  zy,
  input  ny,
  input  f,
  input  no,
  input  [15:0] x,
  input  [15:0] y,
  output [15:0] out,
  output zr,
  output ng
);

  wire add_1_c_o;
  wire [15:0] add_1_s, and_1_out, multiplexer_1_out, multiplexer_2_out, multiplexer_3_out, multiplexer_4_out,
       multiplexer_5_out, not_1_out, not_2_out, not_3_out;

  Multiplexer #(.Bits(16)) multiplexer_1 (.sel(zx), .in_0(x), .in_1({16{1'b0}}), .out(multiplexer_1_out));
  assign not_1_out = ~multiplexer_1_out;  // Not not_1, 16 bits wide
  Multiplexer #(.Bits(16)) multiplexer_2 (
    .sel(nx), .in_0(multiplexer_1_out), .in_1(not_1_out), .out(multiplexer_2_out));
  Multiplexer #(.Bits(16)) multiplexer_3 (.sel(zy), .in_0(y), .in_1({16{1'b0}}), .out(multiplexer_3_out));
  Multiplexer #(.Bits(16)) multiplexer_4 (
    .sel(ny), .in_0(multiplexer_3_out), .in_1(not_2_out), .out(multiplexer_4_out));
  assign not_2_out = ~multiplexer_3_out;  // Not not_2, 16 bits wide
  assign and_1_out = multiplexer_2_out & multiplexer_4_out;  // And and_1, 16 bits wide
  Add #(.Bits(16)) add_1 (.a(multiplexer_2_out), .b(multiplexer_4_out), .c_i(1'b0), .s(add_1_s), .c_o(add_1_c_o));
  Multiplexer #(.Bits(16)) multiplexer_5 (.sel(f), .in_0(and_1_out), .in_1(add_1_s), .out(multiplexer_5_out));
  assign not_3_out = ~multiplexer_5_out;  // Not not_3, 16 bits wide
  Multiplexer #(.Bits(16)) multiplexer_6 (.sel(no), .in_0(multiplexer_5_out), .in_1(not_3_out), .out({ng, out[14:0]}));
  zr zr_1 (.in({ng, out[14:0]}), .out(zr));

  assign out[15] = ng;
endmodule
