// Digital circuit pc.dig as structural Verilog
module pc (
  input  [15:0] in,
  input  inc,
  input  en,
  input  reset,
  input  clock,
  output [15:0] out
);

  wire add_1_c_o;
  wire [15:0] add_1_s, multiplexer_1_out;

  Multiplexer #(.Selector_Bits(3), .Bits(16)) multiplexer_1 (
    .sel({reset, en, inc}), .in_0(out), .in_1(add_1_s), .in_2(in), .in_3(in), .in_4({16{1'b0}}),
    .in_5({16{1'b0}}), .in_6({16{1'b0}}), .in_7({16{1'b0}}), .out(multiplexer_1_out));
  Register #(.Bits(16)) register_1 (.D(multiplexer_1_out), .C(clock), .en(1'b1), .Q(out));
  Add #(.Bits(16)) add_1 (.a(out), .b(16'h1), .c_i(1'b0), .s(add_1_s), .c_o(add_1_c_o));
endmodule
