// Digital circuit zr.dig as structural Verilog
module zr (
  input  [15:0] in,
  output out
);

  wire and_1_out, and_2_out, and_3_out, and_4_out, and_6_out, and_7_out, and_8_out, and_9_out, and_10_out,
       and_11_out, and_12_out, and_13_out, and_14_out, and_15_out, not_1_out, not_2_out, not_3_out,
       not_4_out, not_5_out, not_6_out, not_7_out, not_8_out, not_9_out, not_10_out, not_11_out, not_12_out,
       not_13_out, not_14_out, not_15_out, not_16_out;

  not not_1 (not_1_out, in[0]);
  not not_2 (not_2_out, in[1]);
  not not_3 (not_3_out, in[2]);
  not not_4 (not_4_out, in[3]);
  not not_5 (not_5_out, in[4]);
  not not_6 (not_6_out, in[5]);
  not not_7 (not_7_out, in[6]);
  not not_8 (not_8_out, in[7]);
  not not_9 (not_9_out, in[8]);
  not not_10 (not_10_out, in[9]);
  not not_11 (not_11_out, in[10]);
  not not_12 (not_12_out, in[11]);
  not not_13 (not_13_out, in[12]);
  not not_14 (not_14_out, in[13]);
  not not_15 (not_15_out, in[14]);
  not not_16 (not_16_out, in[15]);
  and and_1 (and_1_out, and_15_out, not_14_out);
  and and_2 (and_2_out, and_1_out, not_15_out);
  and and_3 (and_3_out, not_1_out, not_2_out);
  and and_4 (and_4_out, and_12_out, not_8_out);
  and and_5 (out, and_2_out, not_16_out);
  and and_6 (and_6_out, and_3_out, not_3_out);
  and and_7 (and_7_out, and_9_out, not_5_out);
  and and_8 (and_8_out, and_4_out, not_9_out);
  and and_9 (and_9_out, and_6_out, not_4_out);
  and and_10 (and_10_out, and_7_out, not_6_out);
  and and_11 (and_11_out, and_8_out, not_10_out);
  and and_12 (and_12_out, and_10_out, not_7_out);
  and and_13 (and_13_out, and_11_out, not_11_out);
  and and_14 (and_14_out, and_13_out, not_12_out);
  and and_15 (and_15_out, and_14_out, not_13_out);
endmodule
